// Digital circuit LED.dig as structural Verilog
module LED (
  input  w,
  input  x,
  input  y,
  input  z
);

  wire and_1_out, and_2_out, and_3_out, and_4_out, and_5_out, and_6_out, and_7_out, and_8_out, and_9_out,
       and_10_out, and_11_out, and_12_out, and_13_out, and_14_out, and_15_out, and_16_out, and_17_out,
       and_18_out, not_1_out, not_2_out, not_3_out, not_4_out, or_1_out, or_2_out, or_3_out, or_4_out,
       or_5_out, or_6_out, or_7_out;

  and and_1 (and_1_out, y, not_4_out);
  and and_2 (and_2_out, z, not_1_out);
  and and_3 (and_3_out, x, y);
  and and_4 (and_4_out, w, not_1_out);
  not not_1 (not_1_out, y);
  and and_5 (and_5_out, y, z);
  not not_2 (not_2_out, w);
  not not_3 (not_3_out, x);
  not not_4 (not_4_out, z);
  and and_6 (and_6_out, not_1_out, not_4_out);
  and and_7 (and_7_out, not_4_out, and_4_out);
  and and_8 (and_8_out, y, and_9_out);
  and and_9 (and_9_out, not_2_out, not_3_out);
  and and_10 (and_10_out, not_3_out, z, y);
  and and_11 (and_11_out, not_3_out, and_6_out);
  and and_12 (and_12_out, x, not_1_out);
  and and_13 (and_13_out, and_9_out, not_4_out);
  and and_14 (and_14_out, x, z);
  and and_15 (and_15_out, x, not_2_out);
  and and_16 (and_16_out, and_15_out, and_2_out);
  and and_17 (and_17_out, w, and_12_out);
  and and_18 (and_18_out, not_1_out, not_4_out);
  or or_1 (or_1_out, and_14_out, and_8_out, and_18_out);
  or or_2 (or_2_out, not_1_out, and_1_out, and_15_out);
  or or_3 (or_3_out, and_4_out, and_14_out, and_3_out, and_11_out);
  or or_4 (or_4_out, and_9_out, and_1_out, and_17_out, and_18_out);
  or or_5 (or_5_out, and_4_out, and_14_out, y);
  or or_6 (or_6_out, and_13_out, and_5_out, and_4_out, and_14_out);
  or or_7 (or_7_out, and_11_out, and_16_out, and_7_out, and_10_out);
  Seven_Seg seven_seg_1 (
    .a(or_1_out), .b(or_4_out), .c(or_2_out), .d(or_6_out), .e(or_7_out), .f(or_3_out), .g(or_5_out),
    .dp(1'b0));
endmodule
